# Fritzing sketch lesson3 (saved by Fritzing 0.9.5d)
breadboards: 1

parts:
  パーツ1 = Arduino Uno (Rev3)
  LED1 = smd LED [color="Red (633nm)" package="0603 [SMD]"]
  R1 = Resistor [tolerance=±5% resistance=1k package=THT]
  R2 = Resistor [tolerance=±5% resistance=1k package=THT]
  LED2 = smd LED [color="White (4500K)" package="0603 [SMD]"]

nets:
  N1: パーツ1.D2, R1.Pin_1
  N2: パーツ1.D4, R2.Pin_1
  N3: パーツ1.GND, LED1.anode, LED2.anode
  N4: LED1.cathode, R1.Pin_0
  N5: R2.Pin_0, LED2.cathode
