# Fritzing sketch wire_lesson (saved by Fritzing 0.9.10b)
breadboards: 1

parts:
  Mod1 = KY-022 Infrared Receiver Module [package="Breakout board"]
  パーツ1 = Arduino Uno (Rev3)
  LED1 = LED - 5mm [color="Red (633nm)" current=0.030 package="5 mm [THT]"]
  R1 = Resistor [tolerance=±5% power=0.25 resistance=220 package=THT]

nets:
  N1: Mod1.-, パーツ1.GND, LED1.cathode
  VIN: Mod1.Vin, パーツ1.3V3
  N2: Mod1.S, パーツ1.D2
  N3: パーツ1.D3_PWM, R1.Pin_1
  N4: LED1.anode, R1.Pin_0

custom parts:
  KY-022 Infrared Receiver Module: KY-022 IR receiver module, reacts to 38kHz infrared light.
