# Fritzing sketch wire_lesson (saved by Fritzing 0.9.5d)
breadboards: 1

parts:
  Mod1 = KY-022 Infrared Receiver Module [package="Breakout board"]
  パーツ1 = Arduino Uno (Rev3)

nets:
  N1: Mod1.-, パーツ1.GND
  VIN: Mod1.Vin, パーツ1.3V3
  N2: Mod1.S, パーツ1.D3_PWM

custom parts:
  KY-022 Infrared Receiver Module: KY-022 IR receiver module, reacts to 38kHz infrared light.
