# Fritzing sketch lesson15_2 (saved by Fritzing 0.9.10b)
breadboards: 1

parts:
  パーツ2 = Arduino Uno (Rev3)
  HC-SR04_Sensor_2 = HC-SR04 Ultrasonic Distance Sensor
  LED1 = LED - 5mm [color="Red (633nm)" current=0.030 package="5 mm [THT]"]

nets:
  N1: パーツ2.D9_PWM, LED1.anode
  N2: パーツ2.D2, HC-SR04_Sensor_2.ECHO
  N3: パーツ2.D3_PWM, HC-SR04_Sensor_2.TRIG
  5V: パーツ2.5V, HC-SR04_Sensor_2.VCC
  GND: パーツ2.GND, HC-SR04_Sensor_2.GND, LED1.cathode
